# Fritzing sketch FinalProject (saved by Fritzing 0.9.3b)
breadboards: 1

parts:
  Part1 = Arduino Mega ADK (Rev3)
  hc-sr1 = hc-sr04
  hc-sr2 = hc-sr04
  BT2 = Bluetooth HC-06u [package=THT]
  S1 = Pushbutton [package="[SMD]"]
  LED1 = smd LED [color="Red (633nm)" package="0603 [SMD]"]
  LED2 = smd LED [color="Red (633nm)" package="0603 [SMD]"]
  R1 = Resistor [tolerance=±5% resistance=220 package=THT]
  R2 = Resistor [tolerance=±5% resistance=220 package=THT]

nets:
  N1: Part1.D21/SCL, S1.Pin_1, S1.Pin_2
  N2: Part1.D19/RX1, BT2.TXD
  N3: Part1.D18/TX1, BT2.RXD
  VCC: Part1.5V, hc-sr1.VCC, hc-sr2.VCC, BT2.VCC
  GND: Part1.GND, hc-sr1.GND, hc-sr2.GND, BT2.GND, S1.Pin_3, S1.Pin_4, LED1.cathode, LED2.cathode
  N4: Part1.D22, hc-sr1.Trig
  N5: Part1.D23, hc-sr1.Echo
  N6: Part1.D24, hc-sr2.Trig
  N7: Part1.D25, hc-sr2.Echo
  N8: Part1.D27, R2.Pin_1
  N9: LED1.anode, R2.Pin_0
  N10: LED2.anode, R1.Pin_0

custom parts:
  Bluetooth HC-06u: Bluetooth HC-06 - face up, pins down 16.5mm x 37.5mm PCB
